# Fritzing sketch actuino (saved by Fritzing 0.9.3b)

parts:
  U1 = 2-Channel 5v Relay Shield [package=relay-2ch5v10a]
  Part1 = Arduino Pro Mini v13
  Part2 = I2C Non-Volatile FRAM 32KB
  USBTTL1 = USB TTL Serial Cable
  U2 = Optocoupler [package=THT]
  R1 = Resistor [tolerance=±5% resistance=1k package=THT]
  Fuse1 = Fuse with Handler [part_number=Htc-15m]
  J1 = Screw terminal - 2 pins [package=THT]
  J2 = Screw terminal - 2 pins [package=THT]
  J3 = Screw terminal - 2 pins [package=THT]
  D1 = Diode [package=diode-1n4148]

nets:
  VCC: U1.VCC, Part1.VCC, Part2.VCC, USBTTL1.5V
  GND: U1.GND, Part1.GND, Part2.GND, USBTTL1.GND, U2.Pin_4
  N1: U1.IN1, Part1.D11_PWM/MOSI
  N2: U1.IN2, Part1.D10_PWM/SS
  N3: U1.K1-common, J2.pin1
  N4: U1.K1-NC, U1.K2-NC, J1.pin2, J3.pin1
  N5: U1.K1-NO, U1.K2-NO, Fuse1.Connector1
  N6: U1.K2-common, J2.pin2
  N7: Part1.D0/TX, USBTTL1.RX
  N8: Part1.D1/RX, USBTTL1.TX
  N9: Part1.A4, Part2.SDA
  N10: Part1.A5, Part2.SCL
  N11: Part1.D12/MISO, U2.Pin_5
  N12: U2.Pin_1, R1.Pin_0, D1.C
  N13: U2.Pin_2, J3.pin2, D1.A
  N14: R1.Pin_1, Fuse1.Connector2, J1.pin1

notes:
  12V
  GND
  Motor
  Reed
  reed
  motor
  Instead of the Adafruit FRAM I used a bare MB85RC04V chip (4KB)
  wired like the module
  4N25 actually

custom parts:
  2-Channel 5v Relay Shield: 2 Channel 5v Relay Shield w. 2x SPD-06VDC-SD-C
  I2C Non-Volatile FRAM 32KB: With our I2C FRAM breakout board you can add some FRAM storage to your next DIY project. FRAM allows for a lower power usage and a faster write performance. It's excellent for low-power or inconsistent-power datalogging or data buffering where you want to stream data fast while also keeping the data when there's no power. Unlike Flash or EEPROM there's no pages to worry about. Each byte can be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
